# Fritzing sketch Untitled Sketch 2 (saved by Fritzing 0.9.3b)
breadboards: 1

parts:
  S1 = Pushbutton [package="[THT]"]
  S2 = Pushbutton [package="[THT]"]
  S3 = Pushbutton [package="[THT]"]
  S4 = Pushbutton [package="[THT]"]
  R1 = Resistor [tolerance=±5% resistance=220 package=THT]
  R2 = Resistor [tolerance=±5% resistance=220 package=THT]
  R3 = Resistor [tolerance=±5% resistance=220 package=THT]
  R4 = Resistor [tolerance=±5% resistance=220 package=THT]
  LED1 = LED - 5mm [color="Red (633nm)" package="5 mm [THT]"]
  LED2 = LED - 5mm [color="Red (633nm)" package="5 mm [THT]"]
  LED4 = LED - 5mm [color="Red (633nm)" package="5 mm [THT]"]
  LED3 = LED - 5mm [color="Red (633nm)" package="5 mm [THT]"]
  R5 = Resistor [tolerance=±5% resistance=220 package=THT]
  R6 = Resistor [tolerance=±5% resistance=220 package=THT]
  R7 = Resistor [tolerance=±5% resistance=220 package=THT]
  R8 = Resistor [tolerance=±5% resistance=220 package=THT]
  U1 = HEF4543 [package=dil16]
  U2 = 7-SEGMENT-DISPLAY [package=7-segment-display]  # not connected
  R9 = Resistor [tolerance=±5% resistance=220 package=THT]
  R10 = Resistor [tolerance=±5% resistance=220 package=THT]
  R11 = Resistor [tolerance=±5% resistance=220 package=THT]
  R12 = Resistor [tolerance=±5% resistance=220 package=THT]
  R13 = Resistor [tolerance=±5% resistance=220 package=THT]
  R14 = Resistor [tolerance=±5% resistance=220 package=THT]
  R15 = Resistor [tolerance=±5% resistance=220 package=THT]
  S5 = Pushbutton [package="[THT]"]
  R16 = Resistor [tolerance=±5% resistance=220 package=THT]
  Q1 = NPN-Transistor [package="TO92 [THT]"]
  Part3 = Arduino Uno (Rev3)

nets:
  VCC: S1.Pin_1, S1.Pin_2, S2.Pin_1, S2.Pin_2, S3.Pin_1, S3.Pin_2, S4.Pin_1, S4.Pin_2, U1.LD, U1.VCC, S5.Pin_1, S5.Pin_2, Part3.5V
  N1: S1.Pin_3, S1.Pin_4, R3.Pin_0, Part3.A2
  N2: S2.Pin_3, S2.Pin_4, R4.Pin_0, Part3.A3
  N3: S3.Pin_3, S3.Pin_4, R2.Pin_0, Part3.A4/SDA
  N4: S4.Pin_3, S4.Pin_4, R1.Pin_0, Part3.A5/SCL
  GND: R1.Pin_1, R2.Pin_1, R3.Pin_1, R4.Pin_1, R5.Pin_1, R6.Pin_1, R7.Pin_1, R8.Pin_1, U1.PH, U1.BL, U1.GND, R16.Pin_0, Q1.C, Part3.GND
  N5: LED1.anode, Part3.D2
  N6: LED2.anode, Part3.D3_PWM
  N7: LED4.anode, Part3.D5_PWM
  N8: LED3.anode, Part3.D4
  N9: U1.D2, Part3.D8
  N10: U1.D1, Part3.D7
  N11: U1.D3, Part3.D9_PWM
  N12: U1.D0, Part3.D6_PWM
  N13: U1.A, R10.Pin_1
  N14: U1.B, R9.Pin_1
  N15: U1.C, R12.Pin_1
  N16: U1.D, R14.Pin_0
  N17: U1.E, R11.Pin_0
  N18: U1.G, R13.Pin_0
  N19: U1.F, R15.Pin_0
  N20: S5.Pin_3, S5.Pin_4, R16.Pin_1, Part3.A1
  N21: Q1.B, Part3.A0
